// Logisim project borr.circ as structural Verilog: 3 circuits, main circuit main
module main (
  input  in_1,
  input  in_2,
  input  in_3,
  input  in_4,
  input  [1:0] in_5,
  input  in_6,
  input  in_7,
  input  in_8,
  input  in_9,
  input  [1:0] in_10,
  input  in_11,
  input  [1:0] in_12,
  output [1:0] out_13,
  output out_14,
  output out_15,
  output out_16,
  output out_17,
  output out_18,
  output out_19,
  output out_20,
  output out_21,
  output out_22
);

  Decoder #(.select(2)) decoder_1 (.out0(out_14), .out1(out_15), .out2(out_16), .out3(out_17), .sel(in_5));  // open: en
  Priority_Encoder #(.select(2)) priority_encoder_1 (
    .in0(in_1), .in1(in_2), .in2(in_3), .in3(in_4), .out(out_13));  // open: gs, en_out, en_in
  Demultiplexer #(.select(2)) demultiplexer_1 (
    .out0(out_19), .out1(out_20), .out2(out_21), .out3(out_22), .in(in_11), .sel(in_12));  // open: en
  Multiplexer #(.select(2)) multiplexer_1 (
    .in0(in_6), .in1(in_7), .in2(in_8), .in3(in_9), .out(out_18), .sel(in_10));  // open: en
endmodule

module sumador (
  input  in_1,
  input  in_2,
  input  in_3,
  input  in_4,
  input  in_5,
  input  in_6,
  input  in_7,
  input  in_8,
  input  in_9,
  output out_10,
  output out_11,
  output out_12,
  output out_13,
  output out_14,
  output out_15
);

  wire and_2_out, and_3_out, and_4_out, and_5_out, and_6_out, and_7_out, and_8_out, and_9_out, and_10_out,
       not_1_out, not_2_out, not_3_out, not_4_out, not_5_out, not_6_out;

  not not_1 (not_1_out, in_7);
  not not_2 (not_2_out, in_1);
  not not_3 (not_3_out, in_2);
  not not_4 (not_4_out, in_8);
  and and_1 (out_12, in_1, in_2);
  not not_5 (not_5_out, in_9);
  and and_2 (and_2_out, in_7, in_8);
  and and_3 (and_3_out, in_7, in_9);
  and and_4 (and_4_out, in_8, in_9);
  and and_5 (and_5_out, not_2_out, in_2);
  and and_6 (and_6_out, in_1, not_3_out);
  or or_1 (out_10, and_5_out, and_6_out);
  and and_7 (and_7_out, in_9, in_7, in_8);
  and and_8 (and_8_out, not_1_out, not_4_out, in_9);
  and and_9 (and_9_out, in_7, not_4_out, not_5_out);
  and and_10 (and_10_out, in_8, not_1_out, not_5_out);
  or or_2 (out_15, and_2_out, and_3_out, and_4_out);
  Multiplexer multiplexer_1 (.in0(1'b0), .in1(in_5), .out(out_13), .sel(in_6));  // open: en
  Multiplexer multiplexer_2 (.in0(in_3), .in1(not_6_out), .out(out_11), .sel(in_4));  // open: en
  not not_6 (not_6_out, in_3);
  or or_3 (out_14, and_9_out, and_7_out, and_8_out, and_10_out);
endmodule

module t4 (
  input  R,
  input  S,
  output Q,
  output NO_Q,
  output out_5,
  output out_6
);

  wire clock_1_out;

  Clock clock_1 (.out(clock_1_out));
  nor nor_1 (Q, R, NO_Q);
  nor nor_2 (NO_Q, Q, S);
  S_R_Flip_Flop s_r_ff_1 (.S(S), .clk(clock_1_out), .R(R), .Q(out_5), .Qn(out_6));  // open: preset, reset, en

  // Notes on the sheet:
  //   YOU HAVE TO ENABLE THE CLOCK TO MAKE THE CIRCUIT WORK
endmodule
