// Logisim project 1.3.circ as structural Verilog: 2 circuits, main circuit main
module main (
  input  in_1,
  input  in_2,
  input  in_3,
  input  in_4
);

  wire \versión_1_1_a_2 , \versión_1_1_b_2 , \versión_1_1_c_2 , \versión_1_1_d_2 , \versión_1_1_e ,
       \versión_1_1_f , \versión_1_1_g ;

  \versión_1  \versión_1_1  (
    .A(in_1), .B(in_2), .C(in_3), .D(in_4), .a_2(\versión_1_1_a_2 ), .b_2(\versión_1_1_b_2 ),
    .c_2(\versión_1_1_c_2 ), .d_2(\versión_1_1_d_2 ), .e(\versión_1_1_e ), .f(\versión_1_1_f ),
    .g(\versión_1_1_g ));
  _7_Segment_Display u_7_segment_display_1 (
    .g(\versión_1_1_g ), .f(\versión_1_1_f ), .a(\versión_1_1_a_2 ), .b(\versión_1_1_b_2 ),
    .e(\versión_1_1_e ), .d(\versión_1_1_d_2 ), .c(\versión_1_1_c_2 ));  // open: dp
endmodule

module \versión_1  (
  input  A,
  input  B,
  input  C,
  input  D,
  output a_2,
  output b_2,
  output c_2,
  output d_2,
  output e,
  output f,
  output g
);

  wire and_1_out, and_2_out, and_3_out, and_4_out, and_5_out, and_6_out, and_7_out, and_8_out, and_9_out,
       and_10_out, and_11_out, and_12_out, and_13_out, and_14_out, and_15_out, and_16_out, and_17_out,
       and_18_out, and_19_out, and_20_out, and_21_out, and_22_out, and_23_out, not_1_out, not_2_out,
       not_3_out, not_4_out, not_5_out, not_6_out, not_7_out, not_8_out, not_9_out, not_10_out, not_11_out,
       not_12_out, not_13_out, not_14_out, not_15_out, not_16_out, not_17_out, not_18_out, not_19_out,
       not_20_out, not_21_out, not_22_out, not_23_out, not_24_out, not_25_out, not_26_out, not_27_out,
       not_28_out, not_29_out, not_30_out, not_31_out, not_32_out, not_33_out, not_34_out, not_35_out,
       not_36_out, not_37_out, not_38_out, not_39_out, not_40_out, not_41_out, not_42_out, not_43_out,
       not_44_out, not_45_out, not_46_out, not_47_out, not_48_out, not_49_out, not_50_out, not_51_out,
       not_52_out, not_53_out, not_54_out, not_55_out, not_56_out, not_57_out, not_58_out, not_59_out,
       not_60_out, not_61_out, not_62_out, not_63_out, not_64_out, not_65_out, not_66_out, not_67_out,
       not_68_out, not_69_out, not_70_out, not_71_out, not_72_out, not_73_out, not_74_out, not_75_out,
       not_76_out, not_77_out, not_78_out, not_79_out, not_80_out, not_81_out, not_82_out, not_83_out,
       not_84_out, not_85_out, not_86_out, not_87_out, not_88_out, not_89_out, not_90_out, not_91_out,
       not_92_out, not_93_out, not_94_out, not_95_out, not_96_out, not_97_out, not_98_out, not_99_out,
       not_100_out, not_101_out, not_102_out, not_103_out, not_104_out, not_105_out, not_106_out,
       not_107_out, not_108_out, not_109_out, not_110_out, not_111_out, not_112_out, not_113_out,
       not_114_out, not_115_out, not_116_out, not_117_out, not_118_out, not_119_out, or_1_out, or_2_out,
       or_3_out, or_4_out, or_5_out, or_6_out, or_7_out, or_8_out, or_9_out, or_10_out, or_11_out, or_12_out,
       or_13_out, or_14_out, or_15_out, or_16_out, or_17_out, or_18_out, or_19_out, or_20_out, or_21_out,
       or_22_out, or_23_out;

  not not_1 (not_1_out, D);
  not not_2 (not_2_out, B);
  not not_3 (not_3_out, A);
  not not_4 (not_4_out, C);
  not not_5 (not_5_out, A);
  not not_6 (not_6_out, C);
  not not_7 (not_7_out, D);
  not not_8 (not_8_out, A);
  not not_9 (not_9_out, B);
  not not_10 (not_10_out, A);
  not not_11 (not_11_out, B);
  not not_12 (not_12_out, D);
  not not_13 (not_13_out, A);
  not not_14 (not_14_out, B);
  not not_15 (not_15_out, C);
  not not_16 (not_16_out, A);
  not not_17 (not_17_out, B);
  not not_18 (not_18_out, C);
  not not_19 (not_19_out, D);
  not not_20 (not_20_out, B);
  not not_21 (not_21_out, D);
  not not_22 (not_22_out, B);
  not not_23 (not_23_out, C);
  not not_24 (not_24_out, A);
  not not_25 (not_25_out, C);
  not not_26 (not_26_out, A);
  not not_27 (not_27_out, C);
  not not_28 (not_28_out, D);
  not not_29 (not_29_out, A);
  not not_30 (not_30_out, B);
  not not_31 (not_31_out, A);
  not not_32 (not_32_out, B);
  not not_33 (not_33_out, D);
  not not_34 (not_34_out, A);
  not not_35 (not_35_out, B);
  not not_36 (not_36_out, C);
  not not_37 (not_37_out, A);
  not not_38 (not_38_out, B);
  not not_39 (not_39_out, C);
  not not_40 (not_40_out, D);
  not not_41 (not_41_out, C);
  not not_42 (not_42_out, A);
  not not_43 (not_43_out, C);
  not not_44 (not_44_out, A);
  not not_45 (not_45_out, C);
  not not_46 (not_46_out, D);
  not not_47 (not_47_out, A);
  not not_48 (not_48_out, B);
  not not_49 (not_49_out, A);
  not not_50 (not_50_out, B);
  not not_51 (not_51_out, D);
  not not_52 (not_52_out, A);
  not not_53 (not_53_out, B);
  not not_54 (not_54_out, C);
  not not_55 (not_55_out, A);
  not not_56 (not_56_out, B);
  not not_57 (not_57_out, C);
  not not_58 (not_58_out, D);
  not not_59 (not_59_out, A);
  not not_60 (not_60_out, B);
  not not_61 (not_61_out, C);
  not not_62 (not_62_out, D);
  not not_63 (not_63_out, A);
  not not_64 (not_64_out, B);
  not not_65 (not_65_out, D);
  not not_66 (not_66_out, A);
  not not_67 (not_67_out, B);
  not not_68 (not_68_out, A);
  not not_69 (not_69_out, C);
  not not_70 (not_70_out, A);
  not not_71 (not_71_out, D);
  not not_72 (not_72_out, B);
  not not_73 (not_73_out, C);
  not not_74 (not_74_out, D);
  not not_75 (not_75_out, A);
  not not_76 (not_76_out, B);
  not not_77 (not_77_out, C);
  not not_78 (not_78_out, D);
  not not_79 (not_79_out, A);
  not not_80 (not_80_out, B);
  not not_81 (not_81_out, D);
  not not_82 (not_82_out, A);
  not not_83 (not_83_out, D);
  not not_84 (not_84_out, B);
  not not_85 (not_85_out, C);
  not not_86 (not_86_out, D);
  not not_87 (not_87_out, A);
  not not_88 (not_88_out, B);
  not not_89 (not_89_out, C);
  not not_90 (not_90_out, D);
  not not_91 (not_91_out, A);
  not not_92 (not_92_out, C);
  not not_93 (not_93_out, D);
  not not_94 (not_94_out, A);
  not not_95 (not_95_out, C);
  not not_96 (not_96_out, A);
  not not_97 (not_97_out, D);
  not not_98 (not_98_out, B);
  not not_99 (not_99_out, C);
  not not_100 (not_100_out, D);
  not not_101 (not_101_out, B);
  not not_102 (not_102_out, C);
  not not_103 (not_103_out, A);
  not not_104 (not_104_out, B);
  not not_105 (not_105_out, D);
  not not_106 (not_106_out, A);
  not not_107 (not_107_out, B);
  not not_108 (not_108_out, A);
  not not_109 (not_109_out, C);
  not not_110 (not_110_out, D);
  not not_111 (not_111_out, A);
  not not_112 (not_112_out, C);
  not not_113 (not_113_out, A);
  not not_114 (not_114_out, D);
  not not_115 (not_115_out, B);
  not not_116 (not_116_out, C);
  not not_117 (not_117_out, D);
  not not_118 (not_118_out, B);
  not not_119 (not_119_out, C);
  or or_1 (or_1_out, A, B, C, not_1_out);
  or or_2 (or_2_out, A, not_2_out, C, D);
  or or_3 (or_3_out, not_3_out, B, not_4_out, D);
  or or_4 (or_4_out, not_5_out, B, not_6_out, not_7_out);
  or or_5 (or_5_out, not_8_out, not_9_out, C, D);
  or or_6 (or_6_out, not_10_out, not_11_out, C, not_12_out);
  or or_7 (or_7_out, not_13_out, not_14_out, not_15_out, D);
  or or_8 (or_8_out, not_16_out, not_17_out, not_18_out, not_19_out);
  or or_9 (or_9_out, A, not_20_out, C, not_21_out);
  or or_10 (or_10_out, A, not_22_out, not_23_out, D);
  or or_11 (or_11_out, not_24_out, B, not_25_out, D);
  or or_12 (or_12_out, not_26_out, B, not_27_out, not_28_out);
  or or_13 (or_13_out, not_29_out, not_30_out, C, D);
  or or_14 (or_14_out, not_31_out, not_32_out, C, not_33_out);
  or or_15 (or_15_out, not_34_out, not_35_out, not_36_out, D);
  or or_16 (or_16_out, not_37_out, not_38_out, not_39_out, not_40_out);
  or or_17 (or_17_out, A, B, not_41_out, D);
  or or_18 (or_18_out, not_42_out, B, not_43_out, D);
  or or_19 (or_19_out, not_44_out, B, not_45_out, not_46_out);
  or or_20 (or_20_out, not_47_out, not_48_out, C, D);
  or or_21 (or_21_out, not_49_out, not_50_out, C, not_51_out);
  or or_22 (or_22_out, not_52_out, not_53_out, not_54_out, D);
  or or_23 (or_23_out, not_55_out, not_56_out, not_57_out, not_58_out);
  and and_1 (and_1_out, not_59_out, not_60_out, not_61_out, not_62_out);
  and and_2 (and_2_out, not_63_out, not_64_out, C, not_65_out);
  and and_3 (and_3_out, not_66_out, not_67_out, C, D);
  and and_4 (and_4_out, not_68_out, B, not_69_out, D);
  and and_5 (and_5_out, not_70_out, B, C, not_71_out);
  and and_6 (and_6_out, A, not_72_out, not_73_out, not_74_out);
  and and_7 (and_7_out, not_75_out, not_76_out, not_77_out, not_78_out);
  and and_8 (and_8_out, not_79_out, not_80_out, C, not_81_out);
  and and_9 (and_9_out, not_82_out, B, C, not_83_out);
  and and_10 (and_10_out, A, not_84_out, not_85_out, not_86_out);
  and and_11 (and_11_out, not_87_out, not_88_out, not_89_out, not_90_out);
  and and_12 (and_12_out, not_91_out, B, not_92_out, not_93_out);
  and and_13 (and_13_out, not_94_out, B, not_95_out, D);
  and and_14 (and_14_out, not_96_out, B, C, not_97_out);
  and and_15 (and_15_out, A, not_98_out, not_99_out, not_100_out);
  and and_16 (and_16_out, A, not_101_out, not_102_out, D);
  and and_17 (and_17_out, not_103_out, not_104_out, C, not_105_out);
  and and_18 (and_18_out, not_106_out, not_107_out, C, D);
  and and_19 (and_19_out, not_108_out, B, not_109_out, not_110_out);
  and and_20 (and_20_out, not_111_out, B, not_112_out, D);
  and and_21 (and_21_out, not_113_out, B, C, not_114_out);
  and and_22 (and_22_out, A, not_115_out, not_116_out, not_117_out);
  and and_23 (and_23_out, A, not_118_out, not_119_out, D);
  and and_24 (a_2, or_1_out, or_2_out, or_3_out, or_4_out, or_5_out, or_6_out, or_7_out, or_8_out);
  and and_25 (b_2, or_9_out, or_10_out, or_11_out, or_12_out, or_13_out, or_14_out, or_15_out, or_16_out);
  and and_26 (c_2, or_17_out, or_18_out, or_19_out, or_20_out, or_21_out, or_22_out, or_23_out);
  or or_24 (d_2, and_1_out, and_2_out, and_3_out, and_4_out, and_5_out, and_6_out);
  or or_25 (e, and_7_out, and_8_out, and_9_out, and_10_out);
  or or_26 (f, and_11_out, and_12_out, and_13_out, and_14_out, and_15_out, and_16_out);
  or or_27 (g, and_17_out, and_18_out, and_19_out, and_20_out, and_21_out, and_22_out, and_23_out);
endmodule
