// Logisim project ejercicio 2.3.circ as structural Verilog: 2 circuits, main circuit main
module main (
  input  in_1,
  input  in_2,
  input  in_3,
  input  in_4
);

  wire bcdto7seg_1_a_2, bcdto7seg_1_b_2, bcdto7seg_1_c_2, bcdto7seg_1_d_2, bcdto7seg_1_e, bcdto7seg_1_f,
       bcdto7seg_1_g;

  BCDto7seg bcdto7seg_1 (
    .A(in_1), .B(in_2), .C(in_3), .D(in_4), .a_2(bcdto7seg_1_a_2), .b_2(bcdto7seg_1_b_2),
    .c_2(bcdto7seg_1_c_2), .d_2(bcdto7seg_1_d_2), .e(bcdto7seg_1_e), .f(bcdto7seg_1_f), .g(bcdto7seg_1_g));
  _7_Segment_Display u_7_segment_display_1 (
    .g(bcdto7seg_1_g), .f(bcdto7seg_1_f), .a(bcdto7seg_1_a_2), .b(bcdto7seg_1_b_2), .e(bcdto7seg_1_e),
    .d(bcdto7seg_1_d_2), .c(bcdto7seg_1_c_2));  // open: dp
endmodule

module BCDto7seg (
  input  A,
  input  B,
  input  C,
  input  D,
  output a_2,
  output b_2,
  output c_2,
  output d_2,
  output e,
  output f,
  output g
);

  wire and_1_out, and_2_out, and_3_out, and_4_out, and_5_out, and_6_out, and_7_out, and_8_out, and_9_out,
       and_10_out, and_11_out, and_12_out, and_13_out, and_14_out, and_15_out, and_16_out, and_17_out,
       not_1_out, not_2_out, not_3_out, not_4_out, not_5_out, not_6_out, not_7_out, not_8_out, not_9_out,
       not_10_out, not_11_out, not_12_out, not_13_out, not_14_out, not_15_out, not_16_out, not_17_out,
       not_18_out, not_19_out, not_20_out, not_21_out, not_22_out;

  not not_1 (not_1_out, B);
  and and_1 (and_1_out, not_1_out, not_2_out);
  not not_2 (not_2_out, D);
  and and_2 (and_2_out, B, D);
  not not_3 (not_3_out, B);
  not not_4 (not_4_out, C);
  and and_3 (and_3_out, not_4_out, not_5_out);
  not not_5 (not_5_out, D);
  and and_4 (and_4_out, C, D);
  not not_6 (not_6_out, C);
  not not_7 (not_7_out, A);
  and and_5 (and_5_out, not_7_out, B);
  not not_8 (not_8_out, B);
  and and_6 (and_6_out, not_8_out, not_9_out);
  not not_9 (not_9_out, D);
  not not_10 (not_10_out, B);
  and and_7 (and_7_out, not_10_out, C);
  and and_8 (and_8_out, C, not_11_out);
  not not_11 (not_11_out, D);
  and and_9 (and_9_out, B, not_12_out, D);
  not not_12 (not_12_out, C);
  not not_13 (not_13_out, B);
  and and_10 (and_10_out, not_13_out, not_14_out);
  not not_14 (not_14_out, D);
  and and_11 (and_11_out, C, not_15_out);
  not not_15 (not_15_out, D);
  not not_16 (not_16_out, C);
  and and_12 (and_12_out, not_16_out, not_17_out);
  not not_17 (not_17_out, D);
  and and_13 (and_13_out, B, not_18_out);
  not not_18 (not_18_out, C);
  and and_14 (and_14_out, B, not_19_out);
  not not_19 (not_19_out, D);
  not not_20 (not_20_out, B);
  and and_15 (and_15_out, not_20_out, C);
  and and_16 (and_16_out, B, not_21_out);
  not not_21 (not_21_out, C);
  and and_17 (and_17_out, B, not_22_out);
  not not_22 (not_22_out, D);
  or or_1 (a_2, and_1_out, C, and_2_out, A);
  or or_2 (b_2, not_3_out, and_3_out, and_4_out);
  or or_3 (c_2, not_6_out, D, and_5_out);
  or or_4 (d_2, and_6_out, and_7_out, and_8_out, and_9_out);
  or or_5 (e, and_10_out, and_11_out);
  or or_6 (f, and_12_out, and_13_out, and_14_out, A);
  or or_7 (g, and_15_out, and_16_out, and_17_out, A);
endmodule
