// Logisim project ej4.circ as structural Verilog: 1 circuit, main circuit main
// 0
module main (
  output [3:0] out_1
);

  wire _0_2_out, _0_out, _1_2_out, _1_out, _2_2_out, _2_out, _3_2_out, _3_out, _4_2_out, _4_out, _5_2_out,
       _5_out, _6_2_out, _6_out, _7_2_out, _7_out, _8_2_out, _8_out, _9_2_out, _9_out, nor_1_out;
  wire [3:0] priority_encoder_2_out;

  Button _1 (.out(_1_out));
  Button _4 (.out(_4_out));
  Button _7 (.out(_7_out));
  Button _1_2 (.out(_1_2_out));
  Button _4_2 (.out(_4_2_out));
  Button _7_2 (.out(_7_2_out));
  Button _2 (.out(_2_out));
  Button _5 (.out(_5_out));
  Button _8 (.out(_8_out));
  Button _0 (.out(_0_out));
  Button _2_2 (.out(_2_2_out));
  Button _5_2 (.out(_5_2_out));
  Button _8_2 (.out(_8_2_out));
  Button _0_2 (.out(_0_2_out));
  Button _3 (.out(_3_out));
  Button _6 (.out(_6_out));
  Button _9 (.out(_9_out));
  Button _3_2 (.out(_3_2_out));
  Button _6_2 (.out(_6_2_out));
  Button _9_2 (.out(_9_2_out));
  nor nor_1 (nor_1_out, _0_2_out, _1_2_out, _2_2_out, _3_2_out, _4_2_out, _5_2_out, _6_2_out, _7_2_out, _8_2_out, _9_2_out);
  Priority_Encoder #(.select(4)) priority_encoder_1 (
    .in0(_0_out), .in1(_1_out), .in2(_2_out), .in3(_3_out), .in4(_4_out), .in5(_5_out), .in6(_6_out),
    .in7(_7_out), .in8(_8_out), .in9(_9_out), .out(out_1));  // open: in10, in11, in12, in13, in14, in15, gs, en_out, en_in
  Priority_Encoder #(.select(4)) priority_encoder_2 (
    .in0(_0_2_out), .in1(_1_2_out), .in2(_2_2_out), .in3(_3_2_out), .in4(_4_2_out), .in5(_5_2_out),
    .in6(_6_2_out), .in7(_7_2_out), .in8(_8_2_out), .in9(_9_2_out), .in14(nor_1_out),
    .out(priority_encoder_2_out));  // open: in10, in11, in12, in13, in15, gs, en_out, en_in
  Hex_Digit_Display hex_digit_display_1 (.value(priority_encoder_2_out));  // open: dp
endmodule
