// Logisim project SubproyectoMemoria.circ as structural Verilog: 5 circuits, main circuit Memoria
module Memoria (
  input  [3:0] in_1,
  input  [3:0] in_2,
  input  [3:0] in_3
);

  wire clock_1_out, conv11asignobcd_1_out_5, d_ff_1_q, M_minus_out, M_plus_out, MC_out, Min_out, or_1_out,
       or_2_out, or_3_out, shift_register_1_out;
  wire [3:0] conv11asignobcd_1_out_2, conv11asignobcd_1_out_3, conv11asignobcd_1_out_4;
  wire [10:0] adder_1_out, convbcda11_1_out_4, multiplexer_1_out, multiplexer_2_out, negator_1_out,
       register_1_q;

  Button Min (.out(Min_out));
  Button MC (.out(MC_out));
  Button M_plus (.out(M_plus_out));
  Button M_minus (.out(M_minus_out));
  Hex_Digit_Display hex_digit_display_1 (.value(in_2));  // open: dp
  Hex_Digit_Display hex_digit_display_2 (.value(in_1));  // open: dp
  Hex_Digit_Display hex_digit_display_3 (.value(in_3));  // open: dp
  ConvBCDa11 convbcda11_1 (.out_4(convbcda11_1_out_4), .in_1(in_3), .in_2(in_2), .in_3(in_1));
  LED M (.in(d_ff_1_q));
  _7_Segment_Display u_7_segment_display_1 (.g(conv11asignobcd_1_out_5));  // open: f, a, b, e, d, c, dp
  Hex_Digit_Display hex_digit_display_4 (.value(conv11asignobcd_1_out_3));  // open: dp
  Hex_Digit_Display hex_digit_display_5 (.value(conv11asignobcd_1_out_4));  // open: dp
  Conv11aSignoBCD conv11asignobcd_1 (
    .in_1(register_1_q), .out_2(conv11asignobcd_1_out_2), .out_3(conv11asignobcd_1_out_3),
    .out_4(conv11asignobcd_1_out_4), .out_5(conv11asignobcd_1_out_5));
  Negator #(.width(11)) negator_1 (.in(convbcda11_1_out_4), .out(negator_1_out));
  Hex_Digit_Display hex_digit_display_6 (.value(conv11asignobcd_1_out_2));  // open: dp
  D_Flip_Flop d_ff_1 (.clk(or_1_out), .D(or_1_out), .Q(d_ff_1_q), .reset(MC_out));  // open: Qn, preset, en
  or or_1 (or_1_out, Min_out, M_minus_out, M_minus_out);
  Multiplexer #(.width(11)) multiplexer_1 (
    .in0(convbcda11_1_out_4), .in1(negator_1_out), .out(multiplexer_1_out), .sel(M_minus_out));  // open: en
  Adder #(.width(11)) adder_1 (.a(multiplexer_1_out), .b(register_1_q), .out(adder_1_out));  // open: cin, cout
  or or_2 (or_2_out, M_plus_out, M_minus_out);
  Multiplexer #(.width(11)) multiplexer_2 (
    .in0(convbcda11_1_out_4), .in1(adder_1_out), .out(multiplexer_2_out), .sel(or_2_out));  // open: en
  or or_3 (or_3_out, Min_out, or_2_out);
  Register #(.width(11)) register_1 (
    .D(multiplexer_2_out), .Q(register_1_q), .clk(shift_register_1_out), .clr(MC_out));  // open: en
  Shift_Register #(.length(3)) shift_register_1 (
    .in(or_3_out), .clk(clock_1_out), .out(shift_register_1_out));  // open: shift, load, clr, d0, q0, d1, q1, d2, q2
  Clock clock_1 (.out(clock_1_out));

  // Notes on the sheet:
  //   VISOR ENTRADA
  //   VISOR MEMORIA
endmodule

// Memoria
module ModuloMemoria (
  input  [10:0] Data_IN,
  input  Min,
  input  MC,
  input  M_plus,
  input  M_minus,
  output M,
  output [10:0] Data_OUT
);

  wire clock_1_out, or_1_out, or_2_out, or_3_out, shift_register_1_out;
  wire [10:0] adder_1_out, multiplexer_1_out, multiplexer_2_out, negator_1_out;

  Negator #(.width(11)) negator_1 (.in(Data_IN), .out(negator_1_out));
  D_Flip_Flop d_ff_1 (.clk(or_1_out), .D(or_1_out), .Q(M), .reset(MC));  // open: Qn, preset, en
  or or_1 (or_1_out, Min, M_minus, M_minus);
  Multiplexer #(.width(11)) multiplexer_1 (
    .in0(Data_IN), .in1(negator_1_out), .out(multiplexer_1_out), .sel(M_minus));  // open: en
  Adder #(.width(11)) adder_1 (.a(multiplexer_1_out), .b(Data_OUT), .out(adder_1_out));  // open: cin, cout
  or or_2 (or_2_out, M_plus, M_minus);
  Multiplexer #(.width(11)) multiplexer_2 (
    .in0(Data_IN), .in1(adder_1_out), .out(multiplexer_2_out), .sel(or_2_out));  // open: en
  Register #(.width(11)) register_1 (
    .D(multiplexer_2_out), .Q(Data_OUT), .clk(shift_register_1_out), .clr(MC));  // open: en
  or or_3 (or_3_out, Min, or_2_out);
  Clock clock_1 (.out(clock_1_out));
  Shift_Register #(.length(3)) shift_register_1 (
    .in(or_3_out), .clk(clock_1_out), .out(shift_register_1_out));  // open: shift, load, clr, d0, q0, d1, q1, d2, q2
endmodule

module MemoriaConModulo (
  input  [3:0] in_1,
  input  [3:0] in_2,
  input  [3:0] in_3
);

  wire clock_1_out, conv11asignobcd_1_out_5, d_ff_1_q, M_minus_out, M_plus_out, MC_out, Min_out, or_1_out,
       or_2_out, or_3_out, shift_register_1_out;
  wire [3:0] conv11asignobcd_1_out_2, conv11asignobcd_1_out_3, conv11asignobcd_1_out_4;
  wire [10:0] adder_1_out, convbcda11_1_out_4, multiplexer_1_out, multiplexer_2_out, negator_1_out,
       register_1_q;

  Button Min (.out(Min_out));
  Button MC (.out(MC_out));
  Button M_plus (.out(M_plus_out));
  Button M_minus (.out(M_minus_out));
  Hex_Digit_Display hex_digit_display_1 (.value(in_2));  // open: dp
  Hex_Digit_Display hex_digit_display_2 (.value(in_1));  // open: dp
  Hex_Digit_Display hex_digit_display_3 (.value(in_3));  // open: dp
  ConvBCDa11 convbcda11_1 (.out_4(convbcda11_1_out_4), .in_1(in_3), .in_2(in_2), .in_3(in_1));
  LED M (.in(d_ff_1_q));
  _7_Segment_Display u_7_segment_display_1 (.g(conv11asignobcd_1_out_5));  // open: f, a, b, e, d, c, dp
  Hex_Digit_Display hex_digit_display_4 (.value(conv11asignobcd_1_out_4));  // open: dp
  Hex_Digit_Display hex_digit_display_5 (.value(conv11asignobcd_1_out_3));  // open: dp
  Conv11aSignoBCD conv11asignobcd_1 (
    .in_1(register_1_q), .out_2(conv11asignobcd_1_out_2), .out_3(conv11asignobcd_1_out_3),
    .out_4(conv11asignobcd_1_out_4), .out_5(conv11asignobcd_1_out_5));
  Negator #(.width(11)) negator_1 (.in(convbcda11_1_out_4), .out(negator_1_out));
  Hex_Digit_Display hex_digit_display_6 (.value(conv11asignobcd_1_out_2));  // open: dp
  D_Flip_Flop d_ff_1 (.clk(or_1_out), .D(or_1_out), .Q(d_ff_1_q), .reset(MC_out));  // open: Qn, preset, en
  or or_1 (or_1_out, Min_out, M_minus_out, M_minus_out);
  Multiplexer #(.width(11)) multiplexer_1 (
    .in0(convbcda11_1_out_4), .in1(negator_1_out), .out(multiplexer_1_out), .sel(M_minus_out));  // open: en
  Adder #(.width(11)) adder_1 (.a(multiplexer_1_out), .b(register_1_q), .out(adder_1_out));  // open: cin, cout
  or or_2 (or_2_out, M_plus_out, M_minus_out);
  Multiplexer #(.width(11)) multiplexer_2 (
    .in0(convbcda11_1_out_4), .in1(adder_1_out), .out(multiplexer_2_out), .sel(or_2_out));  // open: en
  or or_3 (or_3_out, Min_out, or_2_out);
  Register #(.width(11)) register_1 (
    .D(multiplexer_2_out), .Q(register_1_q), .clk(shift_register_1_out), .clr(MC_out));  // open: en
  Shift_Register #(.length(3)) shift_register_1 (
    .in(or_3_out), .clk(clock_1_out), .out(shift_register_1_out));  // open: shift, load, clr, d0, q0, d1, q1, d2, q2
  Clock clock_1 (.out(clock_1_out));

  // Notes on the sheet:
  //   VISOR ENTRADA
  //   VISOR MEMORIA
endmodule

module TecladoMod (
  input  MR,
  input  [10:0] Data_IN_MEM,
  input  _7,
  input  _8,
  input  _9,
  input  in_6,
  input  _4,
  input  _5,
  input  _6,
  input  in_10,
  input  _1,
  input  _2,
  input  _3,
  input  in_14,
  input  in_15,
  input  _0,
  input  C,
  output [10:0] Teclado_Data_OUT,
  output TeclaNum
);

  wire d_ff_1_q, or_1_out, priority_encoder_1_gs, t_ff_1_q;
  wire [3:0] priority_encoder_1_out, shift_register_1_q0, shift_register_1_q1, shift_register_1_q2;
  wire [10:0] convbcda11_1_out_4, multiplexer_2_out, negator_1_out;

  or or_1 (or_1_out, C, in_14, in_10, in_6);
  D_Flip_Flop d_ff_1 (.clk(MR), .D(MR), .Q(d_ff_1_q), .reset(or_1_out));  // open: Qn, preset, en
  T_Flip_Flop t_ff_1 (.clk(in_15), .T(in_15), .Q(t_ff_1_q));  // open: Qn, preset, reset, en
  Priority_Encoder #(.select(4)) priority_encoder_1 (
    .in0(_0), .in1(_1), .in2(_2), .in3(_3), .in4(_4), .in5(_5), .in6(_6), .in7(_7), .in8(_8), .in9(_9),
    .out(priority_encoder_1_out), .gs(priority_encoder_1_gs));  // open: in10, in11, in12, in13, in14, in15, en_out, en_in
  Shift_Register #(.width(4), .length(3)) shift_register_1 (
    .in(priority_encoder_1_out), .clk(priority_encoder_1_gs), .clr(or_1_out), .q0(shift_register_1_q0),
    .q1(shift_register_1_q1), .q2(shift_register_1_q2));  // open: shift, out, load, d0, d1, d2
  ConvBCDa11 convbcda11_1 (
    .out_4(convbcda11_1_out_4), .in_1(shift_register_1_q0), .in_2(shift_register_1_q1),
    .in_3(shift_register_1_q2));
  or or_2 (TeclaNum, d_ff_1_q, in_15, priority_encoder_1_gs);
  Multiplexer #(.width(11)) multiplexer_1 (
    .in0(multiplexer_2_out), .in1(Data_IN_MEM), .out(Teclado_Data_OUT), .sel(d_ff_1_q));  // open: en
  Negator #(.width(11)) negator_1 (.in(convbcda11_1_out_4), .out(negator_1_out));
  Multiplexer #(.width(11)) multiplexer_2 (
    .in0(convbcda11_1_out_4), .in1(negator_1_out), .out(multiplexer_2_out), .sel(t_ff_1_q));  // open: en
endmodule

module TecladoSec (
);

  wire _0_out, _1_out, _2_out, _3_out, _4_out, _5_out, _6_out, _7_out, _8_out, _9_out, button_2_out,
       button_3_out, button_4_out, button_out, C_out, conv11asignobcd_1_out_5, M_minus_out, M_plus_out,
       MC_out, Min_out, modulomemoria_1_m, MR_out, tecladomod_1_teclanum;
  wire [3:0] conv11asignobcd_1_out_2, conv11asignobcd_1_out_3, conv11asignobcd_1_out_4;
  wire [10:0] modulomemoria_1_data_out, tecladomod_1_teclado_data_out;

  Button Min (.out(Min_out));
  Button _7 (.out(_7_out));
  Button _4 (.out(_4_out));
  Button _1 (.out(_1_out));
  Button button (.out(button_out));
  Button M_plus (.out(M_plus_out));
  Button M_minus (.out(M_minus_out));
  Button _8 (.out(_8_out));
  Button _9 (.out(_9_out));
  Button _6 (.out(_6_out));
  Button _5 (.out(_5_out));
  Button _3 (.out(_3_out));
  Button _2 (.out(_2_out));
  Button C (.out(C_out));
  Button _0 (.out(_0_out));
  Button MR (.out(MR_out));
  Button MC (.out(MC_out));
  Button button_2 (.out(button_2_out));
  Button button_3 (.out(button_3_out));
  Button button_4 (.out(button_4_out));
  ModuloMemoria modulomemoria_1 (
    .M(modulomemoria_1_m), .Data_IN(tecladomod_1_teclado_data_out), .Data_OUT(modulomemoria_1_data_out),
    .Min(Min_out), .MC(MC_out), .M_plus(M_plus_out), .M_minus(M_minus_out));
  TecladoMod tecladomod_1 (
    .MR(MR_out), ._7(_7_out), ._4(_4_out), ._1(_1_out), ._8(_8_out), ._5(_5_out), ._2(_2_out), ._0(_0_out),
    ._9(_9_out), ._6(_6_out), ._3(_3_out), .C(C_out), .in_6(button_2_out), .in_10(button_3_out),
    .in_14(button_4_out), .Data_IN_MEM(modulomemoria_1_data_out),
    .Teclado_Data_OUT(tecladomod_1_teclado_data_out), .in_15(button_out), .TeclaNum(tecladomod_1_teclanum));
  LED M (.in(modulomemoria_1_m));
  _7_Segment_Display u_7_segment_display_1 (.g(conv11asignobcd_1_out_5));  // open: f, a, b, e, d, c, dp
  LED TeclaNum (.in(tecladomod_1_teclanum));
  Hex_Digit_Display hex_digit_display_1 (.value(conv11asignobcd_1_out_3));  // open: dp
  Hex_Digit_Display hex_digit_display_2 (.value(conv11asignobcd_1_out_4));  // open: dp
  Conv11aSignoBCD conv11asignobcd_1 (
    .in_1(tecladomod_1_teclado_data_out), .out_2(conv11asignobcd_1_out_2), .out_3(conv11asignobcd_1_out_3),
    .out_4(conv11asignobcd_1_out_4), .out_5(conv11asignobcd_1_out_5));
  Hex_Digit_Display hex_digit_display_3 (.value(conv11asignobcd_1_out_2));  // open: dp

  // Notes on the sheet:
  //   TECLADO CALCULADORA
  //   VISOR CALCULADORA
endmodule
