// Logisim project SubproyectoControl.circ as structural Verilog: 5 circuits, main circuit UnidadControl
// Unidad de Control
module UnidadControl (
  input  [1:0] Tipo,
  input  Reloj,
  input  Reset,
  output A_B_prime,
  output Op,
  output T_R_prime
);
endmodule

module Completa (
);

  wire _0_out, _1_out, _2_out, _3_out, _4_out, _5_out, _6_out, _7_out, _8_out, _9_out, button_2_out,
       button_3_out, button_4_out, button_out, C_out, M_minus_out, M_plus_out, MC_out, Min_out,
       modcalc_1_mact, modcalc_1_sg, MR_out;
  wire [3:0] modcalc_1_v0, modcalc_1_v1, modcalc_1_v2;

  LED M (.in(modcalc_1_mact));
  _7_Segment_Display u_7_segment_display_1 (.g(modcalc_1_sg));  // open: f, a, b, e, d, c, dp
  Hex_Digit_Display hex_digit_display_1 (.value(modcalc_1_v2));  // open: dp
  Button M_minus (.out(M_minus_out));
  Button Min (.out(Min_out));
  Button _7 (.out(_7_out));
  Button _8 (.out(_8_out));
  Button _5 (.out(_5_out));
  Button _4 (.out(_4_out));
  Button _2 (.out(_2_out));
  Button _1 (.out(_1_out));
  Button button (.out(button_out));
  Button _0 (.out(_0_out));
  Hex_Digit_Display hex_digit_display_2 (.value(modcalc_1_v1));  // open: dp
  Hex_Digit_Display hex_digit_display_3 (.value(modcalc_1_v0));  // open: dp
  Button M_plus (.out(M_plus_out));
  Button MC (.out(MC_out));
  Button _9 (.out(_9_out));
  Button _6 (.out(_6_out));
  Button _3 (.out(_3_out));
  Button C (.out(C_out));
  Button MR (.out(MR_out));
  Button button_2 (.out(button_2_out));
  Button button_3 (.out(button_3_out));
  Button button_4 (.out(button_4_out));
  ModCalc modcalc_1 (
    .Mact(modcalc_1_mact), .Sg(modcalc_1_sg), .V2(modcalc_1_v2), .V1(modcalc_1_v1), .V0(modcalc_1_v0),
    .Min(Min_out), .M_minus(M_minus_out), .M_plus(M_plus_out), .MC(MC_out), .MR(MR_out), ._7(_7_out),
    ._8(_8_out), ._9(_9_out), .in_9(button_2_out), ._4(_4_out), ._5(_5_out), ._6(_6_out),
    .in_13(button_3_out), ._1(_1_out), ._2(_2_out), ._3(_3_out), .in_17(button_4_out), .in_18(button_out),
    ._0(_0_out), .C(C_out));
endmodule

// Calculadora FC
module ModCalc (
  input  Min,
  input  M_minus,
  input  M_plus,
  input  MC,
  input  MR,
  input  _7,
  input  _8,
  input  _9,
  input  in_9,
  input  _4,
  input  _5,
  input  _6,
  input  in_13,
  input  _1,
  input  _2,
  input  _3,
  input  in_17,
  input  in_18,
  input  _0,
  input  C,
  output Mact,
  output Sg,
  output [3:0] V2,
  output [3:0] V1,
  output [3:0] V0
);

  wire modbus_1_clk, modbus_1_reset, unidadcontrol_1_a_b_prime, unidadcontrol_1_op, unidadcontrol_1_t_r_prime;
  wire [1:0] modbus_1_tipo;
  wire [10:0] alumod_1_aluout, modbus_1_dataaluout, modbus_1_dataoutdisplay, undriven;

  ModBus modbus_1 (
    .MR(MR), .TR(unidadcontrol_1_t_r_prime), .AluIn(alumod_1_aluout),
    .DataOutDisplay(modbus_1_dataoutdisplay), .DataALUOut(modbus_1_dataaluout), .Tipo(modbus_1_tipo),
    .Reset(modbus_1_reset), ._7(_7), ._4(_4), ._1(_1), .in_14(in_18), ._8(_8), ._5(_5), ._2(_2), ._0(_0),
    ._9(_9), ._6(_6), ._3(_3), .C(C), .in_5(in_9), .in_9(in_13), .in_13(in_17), .CLK(modbus_1_clk),
    .MemDataIn(undriven));
  // ModuloMemoria modulomemoria_1: pin names not known; wires that end beside it: Min, MC, M_plus, modbus_1_dataoutdisplay
  AluMod alumod_1 (
    .RESET(modbus_1_reset), .DataIn(modbus_1_dataaluout), .AluOut(alumod_1_aluout),
    .TR(unidadcontrol_1_t_r_prime), .CLK(modbus_1_clk), .AB(unidadcontrol_1_a_b_prime),
    .Op(unidadcontrol_1_op));
  Conv11aSignoBCD conv11asignobcd_1 (.in_1(modbus_1_dataoutdisplay), .out_2(V0), .out_3(V1), .out_4(V2), .out_5(Sg));
  UnidadControl unidadcontrol_1 (
    .Tipo(modbus_1_tipo), .Reloj(modbus_1_clk), .A_B_prime(unidadcontrol_1_a_b_prime),
    .Op(unidadcontrol_1_op), .T_R_prime(unidadcontrol_1_t_r_prime), .Reset(modbus_1_reset));

  // Notes on the sheet:
  //   TECLADO
  //   VISOR CALCULADORA
endmodule

module ModBus (
  input  MR,
  input  _7,
  input  _8,
  input  _9,
  input  in_5,
  input  _4,
  input  _5,
  input  _6,
  input  in_9,
  input  _1,
  input  _2,
  input  _3,
  input  in_13,
  input  in_14,
  input  _0,
  input  C,
  input  TR,
  input  [10:0] AluIn,
  input  [10:0] MemDataIn,
  output [10:0] DataOutDisplay,
  output [10:0] DataALUOut,
  output [1:0] Tipo,
  output Reset,
  output CLK
);

  wire clock_1_out, priority_encoder_1_p1, priority_encoder_1_p5;
  wire [1:0] priority_encoder_1_p3;

  // Priority_Encoder #(.select(2)) priority_encoder_1: pin names not known; wires that end beside it: priority_encoder_1_p1, in_9, priority_encoder_1_p3, in_5, priority_encoder_1_p5, in_13
  Register #(.width(2)) register_1 (
    .D(priority_encoder_1_p3), .Q(Tipo), .clk(priority_encoder_1_p5), .clr(C));  // open: en
  // Probe on Tipo
  Clock clock_1 (.out(clock_1_out));
  TecladoMod tecladomod_1 (
    .MR(MR), ._7(_7), ._4(_4), ._1(_1), ._8(_8), ._5(_5), ._2(_2), ._0(_0), ._9(_9), ._6(_6), ._3(_3), .C(C),
    .in_6(in_5), .in_10(in_9), .in_14(in_13), .Data_IN_MEM(MemDataIn), .Teclado_Data_OUT(DataALUOut),
    .in_15(in_14), .TeclaNum(priority_encoder_1_p1));
  Shift_Register #(.length(3)) shift_register_1 (
    .in(priority_encoder_1_p5), .clk(clock_1_out), .out(CLK));  // open: shift, load, clr, d0, q0, d1, q1, d2, q2
  Multiplexer #(.width(11)) multiplexer_1 (.in0(AluIn), .in1(DataALUOut), .out(DataOutDisplay), .sel(TR));  // open: en

  assign Reset = C;

  // Notes on the sheet:
  //   retardo
  //   3 T
endmodule

module AluMod (
  input  RESET,
  input  [10:0] DataIn,
  input  TR,
  input  AB,
  input  Op,
  input  CLK,
  output [10:0] AluOut
);

  wire and_1_out, or_1_out;
  wire [10:0] adder_1_out, B_q, multiplexer_1_out, multiplexer_2_out, negator_1_out;

  Register #(.width(11)) B (.D(DataIn), .en(and_1_out), .Q(B_q), .clk(CLK), .clr(RESET));
  Negator #(.width(11)) negator_1 (.in(B_q), .out(negator_1_out));
  Multiplexer #(.width(11)) multiplexer_1 (
    .in0(adder_1_out), .in1(DataIn), .out(multiplexer_1_out), .sel(TR));  // open: en
  and and_1 (and_1_out, TR, ~AB);  // AND_Gate
  Multiplexer #(.width(11)) multiplexer_2 (
    .in0(B_q), .in1(negator_1_out), .out(multiplexer_2_out), .sel(Op), .en(1'b1));
  Register #(.width(11)) A (.D(multiplexer_1_out), .en(or_1_out), .Q(AluOut), .clk(CLK), .clr(RESET));
  or or_1 (or_1_out, ~TR, AB);  // OR_Gate
  Adder #(.width(11)) adder_1 (.a(multiplexer_2_out), .b(AluOut), .out(adder_1_out));  // open: cin, cout
endmodule
