// Logisim project borr.circ as structural Verilog
module desp_puertas_logicas (
  input  in_1,
  input  in_2,
  input  in_3,
  input  in_4,
  input  in_5,
  input  in_6,
  input  in_7,
  input  in_8,
  input  in_9,
  input  in_10,
  output out_11,
  output out_12,
  output out_13,
  output out_14,
  output out_15
);

  wire and_1_out, and_2_out, and_3_out, and_4_out, and_5_out;

  and and_1 (and_1_out, in_1, in_6);
  and and_2 (and_2_out, in_2, in_7);
  and and_3 (and_3_out, in_3, in_8);
  or or_1 (out_13, and_1_out, and_2_out, and_3_out, and_4_out, and_5_out);
  and and_4 (and_4_out, in_4, in_9);
  and and_5 (and_5_out, in_5, in_10, in_10);

  // Notes on the sheet:
  //   DESPLAZAMIENTO A LA DERECHA E IZQUIERDA POR PUERTAS LOGICAS
endmodule

module desp_mux (
  input  in_1,
  input  in_2,
  input  in_3,
  input  in_4,
  input  in_5,
  input  in_6,
  input  in_7,
  input  in_8,
  input  [2:0] in_9,
  output out_10,
  output out_11,
  output out_12,
  output out_13,
  output out_14,
  output out_15,
  output out_16,
  output out_17
);

  // OR_Gate or_1 is placed but not wired
  Multiplexer #(.select(3)) multiplexer_1 (
    .in0(in_1), .in1(in_4), .in2(in_5), .in6(in_1), .in7(in_1), .out(out_15), .sel(in_9));  // open: in3, in4, in5, en

  // Notes on the sheet:
  //   DESPLAZAMIENTO A LA DERECHA E IZQUIERDA POR MULTIPLEXORES
endmodule

module sumador_restador (
  input  in_1,
  input  in_2,
  input  in_3,
  input  in_4,
  input  in_5,
  input  in_6,
  input  in_7,
  output SUMA,
  output out_9,
  output out_10,
  output out_11
);

  wire adder_2_cout, and_2_out, and_3_out, not_1_out, not_2_out, xor_1_out, xor_2_out;

  not not_1 (not_1_out, in_1);
  not not_2 (not_2_out, in_2);
  Adder #(.width(1)) adder_1 (.a(in_4), .b(xor_1_out), .cin(adder_2_cout), .cout(out_11));  // open: out
  buf xor_1 (xor_1_out, in_3);  // XOR_Gate
  and and_1 (out_9, in_2, in_1);
  buf xor_2 (xor_2_out, in_5);  // XOR_Gate
  and and_2 (and_2_out, in_1, not_2_out);
  and and_3 (and_3_out, in_2, not_1_out);
  Adder #(.width(1)) adder_2 (.a(xor_2_out), .b(in_6), .out(out_10), .cin(in_7), .cout(adder_2_cout));
  or or_1 (SUMA, and_2_out, and_3_out);

  // Notes on the sheet:
  //   RESTADOR
  //   SEMISUMADOR // HALF ADDER
  //   CARRY // ACARREO
endmodule
